# Fritzing sketch Untitled Sketch1 (saved by Fritzing 0.9.3b)

parts:
  U1 = NodeMCU V1.0
  Part1 = MD13S
  VCC1 = Battery block 9V
  M1 = DC Motor

nets:
  N1: U1.D1, Part1.no_name_yet#connector_PWM1
  N2: U1.D2, Part1.no_name_yet#connector_DIR1
  N3: U1.GND, Part1.no_name_yet#connector_G0
  N4: Part1.no_name_yet#connector_MA1, M1.pin_1
  N5: Part1.no_name_yet#connector_MB1, M1.pin_2
  N6: Part1.no_name_yet#connector_N1, VCC1.+
  N7: Part1.no_name_yet#connector_P1, VCC1.-

custom parts:
  NodeMCU V1.0: ESP8266 based NodeMCU
