# Fritzing sketch diagram (saved by Fritzing 0.9.3b)

parts:
  U1 = NodeMCU V1.0
  Part1 = MD13S
  Part2 = MD13S
  M1 = DC Motor
  M2 = DC Motor
  VCC1 = Battery block 9V

nets:
  N1: U1.D1, Part2.no_name_yet#connector_PWM1
  N2: U1.D2, Part2.no_name_yet#connector_DIR1
  N3: U1.GND, Part1.no_name_yet#connector_G0
  N4: U1.D5, Part1.no_name_yet#connector_PWM1
  N5: U1.D6, Part1.no_name_yet#connector_DIR1
  N6: Part1.no_name_yet#connector_MA1, M1.pin_2
  N7: Part1.no_name_yet#connector_MB1, M1.pin_1
  N8: Part1.no_name_yet#connector_N1, Part2.no_name_yet#connector_N1, VCC1.+
  N9: Part1.no_name_yet#connector_P1, Part2.no_name_yet#connector_P1, VCC1.-
  N10: Part2.no_name_yet#connector_MA1, M2.pin_2
  N11: Part2.no_name_yet#connector_MB1, M2.pin_1

custom parts:
  NodeMCU V1.0: ESP8266 based NodeMCU
